# Fritzing sketch ESP8266RJ45 (saved by Fritzing 0.9.2b)
circuit board: 8.46667cm x 5.64444cm
breadboards: 1

parts:
  Espessif_Serial_Wifi_Modul_1 = ESP8266 ESP01 [part_number=ESP8266 package=THT]
  U1 = Voltage Regulator - Variable [package="TO220 [THT]"]
  U3 = MOC3031-M [package=dil06]
  R1 = Resistor [tolerance=±5% resistance=220 package=THT]
  J1 = MAGJACK [package=magjack]
  R2 = Resistor [tolerance=±5% resistance=220 package=THT]
  R3 = Resistor [tolerance=±5% resistance=220 package=THT]
  J2 = Screw terminal - 2 pins [package=THT]
  R4 = Resistor [tolerance=±5% resistance=4.7k package=THT]
  J3 = screw terminal, 3 pins
  R5 = Resistor [tolerance=±5% resistance=220 package=THT]

nets:
  GND: Espessif_Serial_Wifi_Modul_1.GND, U1.ADJ, U3.2, J1.SHIELD, R2.Pin_0, R3.Pin_0, J2.pin1, J3.pin3
  N1: Espessif_Serial_Wifi_Modul_1.RXD, J1.RD-
  N2: Espessif_Serial_Wifi_Modul_1.TXD, J1.RCT
  N3: Espessif_Serial_Wifi_Modul_1.VCC, U1.OUT, J1.YLED+, R4.Pin_1, J3.pin1, R5.Pin_1
  N4: Espessif_Serial_Wifi_Modul_1.GPIO00, R4.Pin_0, J3.pin2
  N5: Espessif_Serial_Wifi_Modul_1.GPIO02, R1.Pin_1, J1.GLED+
  N6: U1.IN, J1.TD+
  N7: U3.1, R1.Pin_0
  N8: U3.4, J2.pin2
  N9: U3.6, R5.Pin_0
  N10: J1.YLED-, R3.Pin_1
  N11: J1.GLED-, R2.Pin_1

custom parts:
  ESP8266 ESP01: Generic WiFi Module based on the ESP8266 with onboard PCB antenna and UART communications
