# Fritzing sketch SimpleAdapter (saved by Fritzing 0.9.2b)
circuit board: 2.49367cm x 2.69217cm
breadboards: 1

parts:
  ESP--> = double row female pin header, 8 pins [form="♀ (female)"]
  Bboard = female pin header, 8 pins [form="♀ (female)"]

nets:
  N1: ESP-->.pin1, Bboard.pin3
  N2: ESP-->.pin2, Bboard.pin4
  N3: ESP-->.pin3, Bboard.pin5
  N4: ESP-->.pin4, Bboard.pin6
  N5: ESP-->.pin5, Bboard.pin7
  N6: ESP-->.pin6, Bboard.pin8
  N7: ESP-->.pin7, Bboard.pin1
  N8: ESP-->.pin8, Bboard.pin2

notes:
  GND
  GP2
  GP0
  RX
  TX
  CH_PD
  VCC
  RST
