# Fritzing sketch adapterESP8266ES12 (saved by Fritzing 0.9.2b)
circuit board: 10cm x 7cm
breadboards: 1

parts:
  U1 = ESP8266-12 WiFi Module [part_number=ESP8266]
  J1 = female pin header, 8 pins [form="♀ (female)"]
  J2 = female pin header, 8 pins [form="♀ (female)"]
  J3 = female pin header, 8 pins [form="♀ (female)"]
  J4 = female pin header, 8 pins [form="♀ (female)"]
  J5 = female pin header, 8 pins [form="♀ (female)"]
  J6 = female pin header, 8 pins [form="♀ (female)"]
  J7 = female pin header, 8 pins [form="♀ (female)"]
  J8 = female pin header, 8 pins [form="♀ (female)"]
  U2 = ESP8266-12 WiFi Module [part_number=ESP8266]
  J9 = female pin header, 8 pins [form="♀ (female)"]
  J10 = female pin header, 8 pins [form="♀ (female)"]
  J11 = female pin header, 8 pins [form="♀ (female)"]
  J12 = female pin header, 8 pins [form="♀ (female)"]
  U3 = ESP8266-12 WiFi Module [part_number=ESP8266]
  J13 = female pin header, 8 pins [form="♀ (female)"]
  J14 = female pin header, 8 pins [form="♀ (female)"]
  J15 = female pin header, 8 pins [form="♀ (female)"]
  J16 = female pin header, 8 pins [form="♀ (female)"]
  U4 = ESP8266-12 WiFi Module [part_number=ESP8266]

nets:
  N1: U1.GPIO_0, J2.pin5, J3.pin5
  N2: U1.GPIO_16, J1.pin4, J4.pin4
  N3: U1.GPIO_1, J2.pin6, J3.pin6
  N4: U1.CH_PD, J1.pin3, J4.pin3
  N5: U1.GND, J2.pin8, J3.pin8
  N6: U1.TXD, J2.pin1, J3.pin1
  N7: U1.ADC, J1.pin2, J4.pin2
  N8: U1.GPIO_14, J1.pin5, J4.pin5
  N9: U1.GPIO_12, J1.pin6, J4.pin6
  N10: U1.GPIO_13, J1.pin7, J4.pin7
  N11: U1.GPIO_4, J2.pin3, J3.pin3
  N12: U1.GPIO_5, J2.pin4, J3.pin4
  N13: U1.GPIO_15, J2.pin7, J3.pin7
  N14: U1.RESET, J1.pin1, J4.pin1
  N15: U1.RXD, J2.pin2, J3.pin2
  N16: U1.VCC, J1.pin8, J4.pin8
  N17: J5.pin1, J7.pin1, U2.RESET
  N18: J5.pin2, J7.pin2, U2.ADC
  N19: J5.pin3, J7.pin3, U2.CH_PD
  N20: J5.pin4, J7.pin4, U2.GPIO_16
  N21: J5.pin5, J7.pin5, U2.GPIO_14
  N22: J5.pin6, J7.pin6, U2.GPIO_12
  N23: J5.pin7, J7.pin7, U2.GPIO_13
  N24: J5.pin8, J7.pin8, U2.VCC
  N25: J6.pin1, J8.pin1, U2.TXD
  N26: J6.pin2, J8.pin2, U2.RXD
  N27: J6.pin3, J8.pin3, U2.GPIO_4
  N28: J6.pin4, J8.pin4, U2.GPIO_5
  N29: J6.pin5, J8.pin5, U2.GPIO_0
  N30: J6.pin6, J8.pin6, U2.GPIO_1
  N31: J6.pin7, J8.pin7, U2.GPIO_15
  N32: J6.pin8, J8.pin8, U2.GND
  N33: J9.pin1, J11.pin1, U3.RESET
  N34: J9.pin2, J11.pin2, U3.ADC
  N35: J9.pin3, J11.pin3, U3.CH_PD
  N36: J9.pin4, J11.pin4, U3.GPIO_16
  N37: J9.pin5, J11.pin5, U3.GPIO_14
  N38: J9.pin6, J11.pin6, U3.GPIO_12
  N39: J9.pin7, J11.pin7, U3.GPIO_13
  N40: J9.pin8, J11.pin8, U3.VCC
  N41: J10.pin1, J12.pin1, U3.TXD
  N42: J10.pin2, J12.pin2, U3.RXD
  N43: J10.pin3, J12.pin3, U3.GPIO_4
  N44: J10.pin4, J12.pin4, U3.GPIO_5
  N45: J10.pin5, J12.pin5, U3.GPIO_0
  N46: J10.pin6, J12.pin6, U3.GPIO_1
  N47: J10.pin7, J12.pin7, U3.GPIO_15
  N48: J10.pin8, J12.pin8, U3.GND
  N49: J13.pin1, J15.pin1, U4.RESET
  N50: J13.pin2, J15.pin2, U4.ADC
  N51: J13.pin3, J15.pin3, U4.CH_PD
  N52: J13.pin4, J15.pin4, U4.GPIO_16
  N53: J13.pin5, J15.pin5, U4.GPIO_14
  N54: J13.pin6, J15.pin6, U4.GPIO_12
  N55: J13.pin7, J15.pin7, U4.GPIO_13
  N56: J13.pin8, J15.pin8, U4.VCC
  N57: J14.pin1, J16.pin1, U4.TXD
  N58: J14.pin2, J16.pin2, U4.RXD
  N59: J14.pin3, J16.pin3, U4.GPIO_4
  N60: J14.pin4, J16.pin4, U4.GPIO_5
  N61: J14.pin5, J16.pin5, U4.GPIO_0
  N62: J14.pin6, J16.pin6, U4.GPIO_1
  N63: J14.pin7, J16.pin7, U4.GPIO_15
  N64: J14.pin8, J16.pin8, U4.GND

custom parts:
  ESP8266-12 WiFi Module: Generic WiFi Module based on the ESP8266 with onboard PCB antenna and UART communications
