# Fritzing sketch homebrooduino (saved by Fritzing 0.9.2b)
circuit board: 5.86217cm x 4.40618cm
breadboards: 1

parts:
  Relais = Relay [part_number=FRS1B-S package=THT]
  R1 = Resistor [tolerance=±5% resistance=220 package=THT]
  VCC_3v = Battery
  T2 = DS18B20 Temperature Sensor [part_number=DS18B20 package="TO92 [THT]"]
  LD333 = Voltage Regulator - 3.3V [package="TO220 [THT]"]
  IR1 = TSOP312.., 314.. [package=THT]
  VCC_5-12v = Battery block 9V
  ESP8266 = ESP8266 ESP01 [part_number=ESP8266 package=THT]
  U2 = MMA_ACCEL_CONNECTOR [package=1x08]
  Composant1 = HC-SR04 Ultrasonic Rangemeter

nets:
  N1: Relais.COIL1, ESP8266.GPIO00, U2.SLP
  GND: Relais.COIL2, VCC_3v.-, T2.GND, LD333.GND, IR1.GND, VCC_5-12v.-, ESP8266.GND, U2.GND, Composant1.GND
  N2: R1.Pin_0, T2.DQ, ESP8266.GPIO02, U2.VCC
  VCC: R1.Pin_1, VCC_3v.+, T2.+Vdd, LD333.output_voltage, IR1.Vs, ESP8266.VCC, ESP8266.CH_PD, U2.Y, U2.GS1, Composant1.VCC
  N3: LD333.input_voltage, VCC_5-12v.+
  N4: IR1.Data, ESP8266.GPIO16, U2.Z
  N5: ESP8266.RXD, U2.GS2, Composant1.Echo
  N6: ESP8266.TXD, U2.X, Composant1.Trig

notes:
  + (5/12vdc)
  -
  Trig
  Echo
  +3v

custom parts:
  DS18B20 Temperature Sensor: A DS18B20 temperature sensor
  ESP8266 ESP01: Generic WiFi Module based on the ESP8266 with onboard PCB antenna and UART communications
